// Logisim project ALU.circ as structural Verilog: 3 circuits, main circuit main
module main (
  input  in_1,
  input  Ainv,
  input  Binv,
  input  [1:0] op,
  input  [31:0] Input_A,
  input  [31:0] Input_B,
  output [31:0] out_7
);

  wire not_1_out, one_bit_alu_1_out_8, one_bit_alu_2_out_8, one_bit_alu_3_out_8, one_bit_alu_4_out_8,
       one_bit_alu_5_out_8, one_bit_alu_6_out_8, one_bit_alu_7_out_8, one_bit_alu_8_out_8,
       one_bit_alu_9_out_8, one_bit_alu_10_out_8, one_bit_alu_11_out_8, one_bit_alu_12_out_8,
       one_bit_alu_13_out_8, one_bit_alu_14_out_8, one_bit_alu_15_out_8, one_bit_alu_16_out_8,
       one_bit_alu_17_out_8, one_bit_alu_18_out_8, one_bit_alu_19_out_8, one_bit_alu_20_out_8,
       one_bit_alu_21_out_8, one_bit_alu_22_out_8, one_bit_alu_23_out_8, one_bit_alu_24_out_8,
       one_bit_alu_25_out_8, one_bit_alu_26_out_8, one_bit_alu_27_out_8, one_bit_alu_28_out_8,
       one_bit_alu_29_out_8, one_bit_alu_30_out_8, one_bit_alu_31_out_8;
  wire [31:0] adder_1_out, bit_extender_1_out, multiplexer_1_out, one_bit_alu_1_out_7;

  one_bit_ALU one_bit_alu_1 (
    .A(Input_A[0]), .in_6(Input_B[0]), .out_7(one_bit_alu_1_out_7[0]), .Ainv(Ainv), .Binv(Binv), .Cin(in_1),
    .OP(op), .out_8(one_bit_alu_1_out_8));
  one_bit_ALU one_bit_alu_2 (
    .A(Input_A[1]), .in_6(Input_B[1]), .out_7(one_bit_alu_1_out_7[1]), .Ainv(Ainv), .Binv(Binv),
    .Cin(one_bit_alu_1_out_8), .OP(op), .out_8(one_bit_alu_2_out_8));
  one_bit_ALU one_bit_alu_3 (
    .A(Input_A[2]), .in_6(Input_B[2]), .out_7(one_bit_alu_1_out_7[2]), .Ainv(Ainv), .Binv(Binv),
    .Cin(one_bit_alu_2_out_8), .OP(op), .out_8(one_bit_alu_3_out_8));
  one_bit_ALU one_bit_alu_4 (
    .A(Input_A[3]), .in_6(Input_B[3]), .out_7(one_bit_alu_1_out_7[3]), .Ainv(Ainv), .Binv(Binv),
    .Cin(one_bit_alu_3_out_8), .OP(op), .out_8(one_bit_alu_4_out_8));
  one_bit_ALU one_bit_alu_5 (
    .A(Input_A[4]), .in_6(Input_B[4]), .out_7(one_bit_alu_1_out_7[4]), .Ainv(Ainv), .Binv(Binv),
    .Cin(one_bit_alu_4_out_8), .OP(op), .out_8(one_bit_alu_5_out_8));
  one_bit_ALU one_bit_alu_6 (
    .A(Input_A[5]), .in_6(Input_B[5]), .out_7(one_bit_alu_1_out_7[5]), .Ainv(Ainv), .Binv(Binv),
    .Cin(one_bit_alu_5_out_8), .OP(op), .out_8(one_bit_alu_6_out_8));
  one_bit_ALU one_bit_alu_7 (
    .A(Input_A[6]), .in_6(Input_B[6]), .out_7(one_bit_alu_1_out_7[6]), .Ainv(Ainv), .Binv(Binv),
    .Cin(one_bit_alu_6_out_8), .OP(op), .out_8(one_bit_alu_7_out_8));
  one_bit_ALU one_bit_alu_8 (
    .A(Input_A[7]), .in_6(Input_B[7]), .out_7(one_bit_alu_1_out_7[7]), .Ainv(Ainv), .Binv(Binv),
    .Cin(one_bit_alu_7_out_8), .OP(op), .out_8(one_bit_alu_8_out_8));
  one_bit_ALU one_bit_alu_9 (
    .A(Input_A[8]), .in_6(Input_B[8]), .out_7(one_bit_alu_1_out_7[8]), .Ainv(Ainv), .Binv(Binv),
    .Cin(one_bit_alu_8_out_8), .OP(op), .out_8(one_bit_alu_9_out_8));
  one_bit_ALU one_bit_alu_10 (
    .A(Input_A[9]), .in_6(Input_B[9]), .out_7(one_bit_alu_1_out_7[9]), .Ainv(Ainv), .Binv(Binv),
    .Cin(one_bit_alu_9_out_8), .OP(op), .out_8(one_bit_alu_10_out_8));
  one_bit_ALU one_bit_alu_11 (
    .A(Input_A[10]), .in_6(Input_B[10]), .out_7(one_bit_alu_1_out_7[10]), .Ainv(Ainv), .Binv(Binv),
    .Cin(one_bit_alu_10_out_8), .OP(op), .out_8(one_bit_alu_11_out_8));
  one_bit_ALU one_bit_alu_12 (
    .A(Input_A[11]), .in_6(Input_B[11]), .out_7(one_bit_alu_1_out_7[11]), .Ainv(Ainv), .Binv(Binv),
    .Cin(one_bit_alu_11_out_8), .OP(op), .out_8(one_bit_alu_12_out_8));
  one_bit_ALU one_bit_alu_13 (
    .A(Input_A[12]), .in_6(Input_B[12]), .out_7(one_bit_alu_1_out_7[12]), .Ainv(Ainv), .Binv(Binv),
    .Cin(one_bit_alu_12_out_8), .OP(op), .out_8(one_bit_alu_13_out_8));
  one_bit_ALU one_bit_alu_14 (
    .A(Input_A[13]), .in_6(Input_B[13]), .out_7(one_bit_alu_1_out_7[13]), .Ainv(Ainv), .Binv(Binv),
    .Cin(one_bit_alu_13_out_8), .OP(op), .out_8(one_bit_alu_14_out_8));
  one_bit_ALU one_bit_alu_15 (
    .A(Input_A[14]), .in_6(Input_B[14]), .out_7(one_bit_alu_1_out_7[14]), .Ainv(Ainv), .Binv(Binv),
    .Cin(one_bit_alu_14_out_8), .OP(op), .out_8(one_bit_alu_15_out_8));
  one_bit_ALU one_bit_alu_16 (
    .A(Input_A[15]), .in_6(Input_B[15]), .out_7(one_bit_alu_1_out_7[15]), .Ainv(Ainv), .Binv(Binv),
    .Cin(one_bit_alu_15_out_8), .OP(op), .out_8(one_bit_alu_16_out_8));
  one_bit_ALU one_bit_alu_17 (
    .A(Input_A[16]), .in_6(Input_B[16]), .out_7(one_bit_alu_1_out_7[16]), .Ainv(Ainv), .Binv(Binv),
    .Cin(one_bit_alu_16_out_8), .OP(op), .out_8(one_bit_alu_17_out_8));
  one_bit_ALU one_bit_alu_18 (
    .A(Input_A[17]), .in_6(Input_B[17]), .out_7(one_bit_alu_1_out_7[17]), .Ainv(Ainv), .Binv(Binv),
    .Cin(one_bit_alu_17_out_8), .OP(op), .out_8(one_bit_alu_18_out_8));
  one_bit_ALU one_bit_alu_19 (
    .A(Input_A[18]), .in_6(Input_B[18]), .out_7(one_bit_alu_1_out_7[18]), .Ainv(Ainv), .Binv(Binv),
    .Cin(one_bit_alu_18_out_8), .OP(op), .out_8(one_bit_alu_19_out_8));
  one_bit_ALU one_bit_alu_20 (
    .A(Input_A[19]), .in_6(Input_B[19]), .out_7(one_bit_alu_1_out_7[19]), .Ainv(Ainv), .Binv(Binv),
    .Cin(one_bit_alu_19_out_8), .OP(op), .out_8(one_bit_alu_20_out_8));
  one_bit_ALU one_bit_alu_21 (
    .A(Input_A[20]), .in_6(Input_B[20]), .out_7(one_bit_alu_1_out_7[20]), .Ainv(Ainv), .Binv(Binv),
    .Cin(one_bit_alu_20_out_8), .OP(op), .out_8(one_bit_alu_21_out_8));
  one_bit_ALU one_bit_alu_22 (
    .A(Input_A[21]), .in_6(Input_B[21]), .out_7(one_bit_alu_1_out_7[21]), .Ainv(Ainv), .Binv(Binv),
    .Cin(one_bit_alu_21_out_8), .OP(op), .out_8(one_bit_alu_22_out_8));
  one_bit_ALU one_bit_alu_23 (
    .A(Input_A[22]), .in_6(Input_B[22]), .out_7(one_bit_alu_1_out_7[22]), .Ainv(Ainv), .Binv(Binv),
    .Cin(one_bit_alu_22_out_8), .OP(op), .out_8(one_bit_alu_23_out_8));
  one_bit_ALU one_bit_alu_24 (
    .A(Input_A[23]), .in_6(Input_B[23]), .out_7(one_bit_alu_1_out_7[23]), .Ainv(Ainv), .Binv(Binv),
    .Cin(one_bit_alu_23_out_8), .OP(op), .out_8(one_bit_alu_24_out_8));
  one_bit_ALU one_bit_alu_25 (
    .A(Input_A[24]), .in_6(Input_B[24]), .out_7(one_bit_alu_1_out_7[24]), .Ainv(Ainv), .Binv(Binv),
    .Cin(one_bit_alu_24_out_8), .OP(op), .out_8(one_bit_alu_25_out_8));
  one_bit_ALU one_bit_alu_26 (
    .A(Input_A[25]), .in_6(Input_B[25]), .out_7(one_bit_alu_1_out_7[25]), .Ainv(Ainv), .Binv(Binv),
    .Cin(one_bit_alu_25_out_8), .OP(op), .out_8(one_bit_alu_26_out_8));
  one_bit_ALU one_bit_alu_27 (
    .A(Input_A[26]), .in_6(Input_B[26]), .out_7(one_bit_alu_1_out_7[26]), .Ainv(Ainv), .Binv(Binv),
    .Cin(one_bit_alu_26_out_8), .OP(op), .out_8(one_bit_alu_27_out_8));
  one_bit_ALU one_bit_alu_28 (
    .A(Input_A[27]), .in_6(Input_B[27]), .out_7(one_bit_alu_1_out_7[27]), .Ainv(Ainv), .Binv(Binv),
    .Cin(one_bit_alu_27_out_8), .OP(op), .out_8(one_bit_alu_28_out_8));
  one_bit_ALU one_bit_alu_29 (
    .A(Input_A[28]), .in_6(Input_B[28]), .out_7(one_bit_alu_1_out_7[28]), .Ainv(Ainv), .Binv(Binv),
    .Cin(one_bit_alu_28_out_8), .OP(op), .out_8(one_bit_alu_29_out_8));
  one_bit_ALU one_bit_alu_30 (
    .A(Input_A[29]), .in_6(Input_B[29]), .out_7(one_bit_alu_1_out_7[29]), .Ainv(Ainv), .Binv(Binv),
    .Cin(one_bit_alu_29_out_8), .OP(op), .out_8(one_bit_alu_30_out_8));
  one_bit_ALU one_bit_alu_31 (
    .A(Input_A[30]), .in_6(Input_B[30]), .out_7(one_bit_alu_1_out_7[30]), .Ainv(Ainv), .Binv(Binv),
    .Cin(one_bit_alu_30_out_8), .OP(op), .out_8(one_bit_alu_31_out_8));
  one_bit_ALU one_bit_alu_32 (
    .A(Input_A[31]), .in_6(Input_B[31]), .out_7(one_bit_alu_1_out_7[31]), .Ainv(Ainv), .Binv(Binv),
    .Cin(one_bit_alu_31_out_8), .OP(op));  // open: out_8
  assign bit_extender_1_out = {{31{1'b0}}, not_1_out};  // Bit_Extender bit_extender_1
  not not_1 (not_1_out, one_bit_alu_31_out_8);
  Multiplexer #(.width(32)) multiplexer_1 (
    .in0(one_bit_alu_1_out_7), .in1(adder_1_out), .out(multiplexer_1_out), .sel(Binv));  // open: en
  Adder #(.width(32)) adder_1 (.a(one_bit_alu_1_out_7), .b(32'h1), .out(adder_1_out));  // open: cin, cout
  Multiplexer #(.select(2), .width(32)) multiplexer_2 (
    .in0(one_bit_alu_1_out_7), .in1(one_bit_alu_1_out_7), .in2(multiplexer_1_out), .in3(bit_extender_1_out),
    .out(out_7), .sel(op));  // open: en
endmodule

// ALU1
module one_bit_ALU (
  input  Ainv,
  input  Binv,
  input  Cin,
  input  [1:0] OP,
  input  A,
  input  in_6,
  output out_7,
  output out_8
);

  wire and_1_out, multiplexer_1_out, multiplexer_2_out, not_1_out, not_2_out, one_bit_adder_1_sun, or_1_out;

  Multiplexer multiplexer_1 (.in0(A), .in1(not_1_out), .out(multiplexer_1_out), .sel(Ainv));  // open: en
  not not_1 (not_1_out, A);
  Multiplexer multiplexer_2 (.in0(in_6), .in1(not_2_out), .out(multiplexer_2_out), .sel(Binv));  // open: en
  not not_2 (not_2_out, in_6);
  one_bit_adder one_bit_adder_1 (
    .sun(one_bit_adder_1_sun), .Cout(out_8), .A(multiplexer_1_out), .B(Cin), .C(multiplexer_2_out));
  and and_1 (and_1_out, multiplexer_1_out, multiplexer_2_out);
  or or_1 (or_1_out, multiplexer_1_out, multiplexer_2_out);
  Multiplexer #(.select(2)) multiplexer_3 (
    .in0(and_1_out), .in1(or_1_out), .in2(one_bit_adder_1_sun), .in3(1'b0), .out(out_7), .sel(OP));  // open: en
endmodule

module one_bit_adder (
  input  A,
  input  B,
  input  C,
  output sun,
  output Cout
);

  wire and_1_out, and_2_out, xor_1_out;

  xor xor_1 (xor_1_out, A, B);
  xor xor_2 (sun, xor_1_out, C);
  and and_1 (and_1_out, xor_1_out, C);
  and and_2 (and_2_out, B, A);
  xor xor_3 (Cout, and_1_out, and_2_out);
endmodule
