// Logisim project CPU_Design.circ as structural Verilog: 4 circuits, main circuit main
module main (
);

  wire and_1_out, and_2_out, clock_1_out, clock_2_out, clock_3_out, control_1_alusrc, control_1_beq,
       control_1_bne, control_1_memtoreg, control_1_memwrite, control_1_regdst, control_1_regwrite,
       my_alu_1_out_6, not_1_out, or_1_out, RST;
  wire [3:0] control_1_out_3;
  wire [4:0] multiplexer_2_out;
  wire [9:0] my_alu_1_out_4_2;
  wire [31:0] adder_1_out, bit_extender_1_out, Instruction_Memory_data, multiplexer_1_out, multiplexer_3_out,
       multiplexer_4_out, my_alu_1_out_4, pc_q, ram_1_data, register_1_r1, register_1_r2;

  Button button_1 (.out(RST));
  Multiplexer #(.select(1), .width(32), .disabled("Z"), .enable("false")) multiplexer_1 (
    .in0(adder_1_out), .in1(bit_extender_1_out), .out(multiplexer_1_out), .sel(or_1_out));
  Register #(.width(32), .trigger("falling"), .Select("high")) pc (
    .D(multiplexer_1_out), .Q(pc_q), .clk(clock_1_out), .clr(RST));  // open: en
  Clock #(.highDuration(1), .lowDuration(1)) clock_1 (.out(clock_1_out));
  Adder #(.width(32)) adder_1 (.a(pc_q), .b(32'h4), .out(adder_1_out));  // open: cin, cout
  ROM #(.addrWidth(10), .dataWidth(32), .Select("low")) Instruction_Memory (
    .addr(pc_q[11:2]), .data(Instruction_Memory_data));
  control control_1 (
    .OP(Instruction_Memory_data[31:26]), .func(Instruction_Memory_data[5:0]), .out_3(control_1_out_3),
    .RegDst(control_1_regdst), .RegWrite(control_1_regwrite), .MemToReg(control_1_memtoreg),
    .MemWrite(control_1_memwrite), .AluSrc(control_1_alusrc), .Beq(control_1_beq), .Bne(control_1_bne));  // open: Halt
  Multiplexer #(.select(1), .width(5), .disabled("Z"), .enable("false")) multiplexer_2 (
    .in0(Instruction_Memory_data[20:16]), .in1(Instruction_Memory_data[15:11]), .out(multiplexer_2_out),
    .sel(control_1_regdst));
  assign bit_extender_1_out = {{16{Instruction_Memory_data[15]}}, Instruction_Memory_data[15:0]};  // Bit_Extender bit_extender_1
  register register_1 (
    .R1(register_1_r1), .R2(register_1_r2), .WE(control_1_regwrite), .Clk(clock_2_out),
    .Rs(Instruction_Memory_data[25:21]), .Rt(Instruction_Memory_data[20:16]), .Din(multiplexer_4_out),
    .Rd(multiplexer_2_out));
  Clock #(.highDuration(1), .lowDuration(1)) clock_2 (.out(clock_2_out));
  Multiplexer #(.select(1), .width(32), .disabled("Z"), .enable("false")) multiplexer_3 (
    .in0(register_1_r2), .in1(bit_extender_1_out), .out(multiplexer_3_out), .sel(control_1_alusrc));
  not not_1 (not_1_out, my_alu_1_out_6);
  My_ALU my_alu_1 (
    .X(register_1_r1), .Y(multiplexer_3_out), .in_3(control_1_out_3),
    .out_4({my_alu_1_out_4[31:12], my_alu_1_out_4_2, my_alu_1_out_4[1:0]}), .out_6(my_alu_1_out_6));  // open: out_5
  and and_1 (and_1_out, control_1_beq, my_alu_1_out_6);
  and and_2 (and_2_out, control_1_bne, not_1_out);
  or or_1 (or_1_out, and_1_out, and_2_out);
  Clock #(.highDuration(1), .lowDuration(1)) clock_3 (.out(clock_3_out));
  RAM #(.addrWidth(10), .dataWidth(32), .bus("separate"), .Select("high")) ram_1 (
    .addr(my_alu_1_out_4_2), .din(register_1_r2), .data(ram_1_data), .str(control_1_memwrite),
    .clk(clock_3_out), .clr(RST));  // open: sel, ld
  Multiplexer #(.select(1), .width(32), .disabled("Z"), .enable("false")) multiplexer_4 (
    .in0({my_alu_1_out_4[31:12], my_alu_1_out_4_2, my_alu_1_out_4[1:0]}), .in1(ram_1_data),
    .out(multiplexer_4_out), .sel(control_1_memtoreg));

  // Notes on the sheet:
  //   contents of Instruction_Memory (hex, n*v repeats v):
  //   20000001 acc00000 8c270000 10070000
endmodule

module control (
  input  [5:0] OP,
  input  [5:0] func,
  output [3:0] out_3,
  output RegDst,
  output RegWrite,
  output MemToReg,
  output MemWrite,
  output AluSrc,
  output Beq,
  output Bne,
  output Halt
);

  wire ADD, ADDI, and_5_out, comparator_6_eq, comparator_7_eq, comparator_8_eq, comparator_9_eq,
       comparator_10_eq, comparator_11_eq, not_1_out, or_2_out, SLT;

  Comparator #(.width(6), .mode("twosComplement")) comparator_1 (.a(OP), .b(6'b100011), .eq(MemToReg));  // open: gt, lt
  Comparator #(.width(6), .mode("twosComplement")) comparator_2 (.a(OP), .b(6'b101011), .eq(MemWrite));  // open: gt, lt
  Comparator #(.width(6), .mode("twosComplement")) comparator_3 (.a(OP), .b(6'b000100), .eq(Beq));  // open: gt, lt
  Comparator #(.width(6), .mode("twosComplement")) comparator_4 (.a(OP), .b(6'b000101), .eq(Bne));  // open: gt, lt
  Comparator #(.width(6), .mode("twosComplement")) comparator_5 (.a(OP), .b(6'b001000), .eq(ADDI));  // open: gt, lt
  Comparator #(.width(6), .mode("twosComplement")) comparator_6 (
    .a(OP), .b({6{1'b0}}), .eq(comparator_6_eq));  // open: gt, lt
  or or_1 (RegWrite, ADDI, RegDst, MemToReg);
  or or_2 (or_2_out, ADD, SLT);
  not not_1 (not_1_out, Halt);
  Comparator #(.width(6), .mode("twosComplement")) comparator_7 (
    .a(func), .b(6'b100000), .eq(comparator_7_eq));  // open: gt, lt
  Comparator #(.width(6), .mode("twosComplement")) comparator_8 (
    .a(func), .b(6'b101010), .eq(comparator_8_eq));  // open: gt, lt
  Comparator #(.width(6), .mode("twosComplement")) comparator_9 (
    .a(func), .b(6'b001100), .eq(comparator_9_eq));  // open: gt, lt
  and and_1 (RegDst, or_2_out, not_1_out);
  and and_2 (ADD, comparator_7_eq, comparator_6_eq);
  and and_3 (SLT, comparator_8_eq, comparator_6_eq);
  and and_4 (Halt, comparator_9_eq, comparator_6_eq);
  or or_3 (AluSrc, MemToReg, ADDI, MemWrite);
  Comparator #(.width(6), .mode("twosComplement")) comparator_10 (
    .a(OP), .b({6{1'b0}}), .eq(comparator_10_eq));  // open: gt, lt
  Comparator #(.width(6), .mode("twosComplement")) comparator_11 (
    .a(func), .b(6'b101010), .eq(comparator_11_eq));  // open: gt, lt
  and and_5 (and_5_out, comparator_10_eq, comparator_11_eq);
  Multiplexer #(.select(1), .width(4), .disabled("Z"), .enable("false")) multiplexer_1 (
    .in0(4'b0101), .in1(4'b1011), .out(out_3), .sel(and_5_out));

  // Other names for the same wires on the sheet: ALU_op[3:0] = out_3; LW = MemToReg; R_type = RegDst; SW = MemWrite;
  //   SysCall = Halt

  // Notes on the sheet:
  //   INSTRUCTION DECODING LOGIC
  //   控制信号
endmodule

module register (
  input  [4:0] Rd,
  input  Clk,
  input  [4:0] Rs,
  input  [31:0] Din,
  input  WE,
  input  [4:0] Rt,
  output [31:0] R1,
  output [31:0] R2
);

  wire demultiplexer_2_out0, demultiplexer_2_out1, demultiplexer_2_out2, demultiplexer_2_out3,
       demultiplexer_2_out4, demultiplexer_2_out5, demultiplexer_2_out6, demultiplexer_2_out7,
       demultiplexer_2_out8;
  wire [31:0] demultiplexer_1_out0, demultiplexer_1_out1, demultiplexer_1_out2, demultiplexer_1_out3,
       demultiplexer_1_out4, demultiplexer_1_out5, demultiplexer_1_out6, demultiplexer_1_out7,
       demultiplexer_1_out8, register_1_q, register_2_q, register_3_q, register_4_q, register_5_q,
       register_6_q, register_7_q, register_8_q;

  Demultiplexer #(.select(5), .width(32), .tristate("false"), .disabled("Z"), .enable("false")) demultiplexer_1 (
    .out0(demultiplexer_1_out0), .out1(demultiplexer_1_out1), .out2(demultiplexer_1_out2),
    .out3(demultiplexer_1_out3), .out4(demultiplexer_1_out4), .out5(demultiplexer_1_out5),
    .out6(demultiplexer_1_out6), .out7(demultiplexer_1_out7), .out8(demultiplexer_1_out8),
    .out9(demultiplexer_1_out8), .out10(demultiplexer_1_out8), .out11(demultiplexer_1_out8),
    .out12(demultiplexer_1_out8), .out13(demultiplexer_1_out8), .out14(demultiplexer_1_out8),
    .out15(demultiplexer_1_out8), .out16(demultiplexer_1_out8), .out17(demultiplexer_1_out8),
    .out18(demultiplexer_1_out8), .out19(demultiplexer_1_out8), .out20(demultiplexer_1_out8),
    .out21(demultiplexer_1_out8), .out22(demultiplexer_1_out8), .out23(demultiplexer_1_out8),
    .out24(demultiplexer_1_out8), .out25(demultiplexer_1_out8), .out26(demultiplexer_1_out8),
    .out27(demultiplexer_1_out8), .out28(demultiplexer_1_out8), .out29(demultiplexer_1_out8),
    .out30(demultiplexer_1_out8), .out31(demultiplexer_1_out8), .in(Din), .sel(Rd));
  Demultiplexer #(.select(5), .width(1), .tristate("false"), .disabled("Z"), .enable("false")) demultiplexer_2 (
    .out0(demultiplexer_2_out0), .out1(demultiplexer_2_out1), .out2(demultiplexer_2_out2),
    .out3(demultiplexer_2_out3), .out4(demultiplexer_2_out4), .out5(demultiplexer_2_out5),
    .out6(demultiplexer_2_out6), .out7(demultiplexer_2_out7), .out8(demultiplexer_2_out8),
    .out9(demultiplexer_2_out8), .out10(demultiplexer_2_out8), .out11(demultiplexer_2_out8),
    .out12(demultiplexer_2_out8), .out13(demultiplexer_2_out8), .out14(demultiplexer_2_out8),
    .out15(demultiplexer_2_out8), .out16(demultiplexer_2_out8), .out17(demultiplexer_2_out8),
    .out18(demultiplexer_2_out8), .out19(demultiplexer_2_out8), .out20(demultiplexer_2_out8),
    .out21(demultiplexer_2_out8), .out22(demultiplexer_2_out8), .out23(demultiplexer_2_out8),
    .out24(demultiplexer_2_out8), .out25(demultiplexer_2_out8), .out26(demultiplexer_2_out8),
    .out27(demultiplexer_2_out8), .out28(demultiplexer_2_out8), .out29(demultiplexer_2_out8),
    .out30(demultiplexer_2_out8), .out31(demultiplexer_2_out8), .in(WE), .sel(Rd));
  Register #(.width(32), .trigger("falling"), .Select("high")) register_1 (
    .D(demultiplexer_1_out0), .en(demultiplexer_2_out0), .Q(register_1_q), .clk(Clk));  // open: clr
  Register #(.width(32), .trigger("falling"), .Select("high")) register_2 (
    .D(demultiplexer_1_out1), .en(demultiplexer_2_out1), .Q(register_2_q), .clk(Clk));  // open: clr
  Register #(.width(32), .trigger("falling"), .Select("high")) register_3 (
    .D(demultiplexer_1_out2), .en(demultiplexer_2_out2), .Q(register_3_q), .clk(Clk));  // open: clr
  Register #(.width(32), .trigger("falling"), .Select("high")) register_4 (
    .D(demultiplexer_1_out3), .en(demultiplexer_2_out3), .Q(register_4_q), .clk(Clk));  // open: clr
  Register #(.width(32), .trigger("falling"), .Select("high")) register_5 (
    .D(demultiplexer_1_out4), .en(demultiplexer_2_out4), .Q(register_5_q), .clk(Clk));  // open: clr
  Register #(.width(32), .trigger("falling"), .Select("high")) register_6 (
    .D(demultiplexer_1_out5), .en(demultiplexer_2_out5), .Q(register_6_q), .clk(Clk));  // open: clr
  Register #(.width(32), .trigger("falling"), .Select("high")) register_7 (
    .D(demultiplexer_1_out6), .en(demultiplexer_2_out6), .Q(register_7_q), .clk(Clk));  // open: clr
  Register #(.width(32), .trigger("falling"), .Select("high")) register_8 (
    .D(demultiplexer_1_out7), .en(demultiplexer_2_out7), .Q(register_8_q), .clk(Clk));  // open: clr
  Multiplexer #(.select(5), .width(32), .disabled("Z"), .enable("false")) multiplexer_1 (
    .in0(register_1_q), .in1(register_2_q), .in2(register_3_q), .in3(register_4_q), .in4(register_5_q),
    .in5(register_6_q), .in6(register_7_q), .in7(register_8_q), .in8(register_5_q), .in9(register_5_q),
    .in10(register_5_q), .in11(register_5_q), .in12(register_5_q), .in13(register_5_q), .in14(register_5_q),
    .in15(register_5_q), .in16(register_5_q), .in17(register_5_q), .in18(register_5_q), .in19(register_5_q),
    .in20(register_5_q), .in21(register_5_q), .in22(register_5_q), .in23(register_5_q), .in24(register_5_q),
    .in25(register_5_q), .in26(register_5_q), .in27(register_5_q), .in28(register_5_q), .in29(register_5_q),
    .in30(register_5_q), .in31(register_5_q), .out(R1), .sel(Rs));
  Multiplexer #(.select(5), .width(32), .disabled("Z"), .enable("false")) multiplexer_2 (
    .in0(register_1_q), .in1(register_2_q), .in2(register_3_q), .in3(register_4_q), .in4(register_5_q),
    .in5(register_6_q), .in6(register_7_q), .in7(register_8_q), .in8({32{1'b0}}), .in9({32{1'b0}}),
    .in10({32{1'b0}}), .in11({32{1'b0}}), .in12({32{1'b0}}), .in13({32{1'b0}}), .in14({32{1'b0}}),
    .in15({32{1'b0}}), .in16({32{1'b0}}), .in17({32{1'b0}}), .in18({32{1'b0}}), .in19({32{1'b0}}),
    .in20({32{1'b0}}), .in21({32{1'b0}}), .in22({32{1'b0}}), .in23({32{1'b0}}), .in24({32{1'b0}}),
    .in25({32{1'b0}}), .in26({32{1'b0}}), .in27({32{1'b0}}), .in28({32{1'b0}}), .in29({32{1'b0}}),
    .in30({32{1'b0}}), .in31({32{1'b0}}), .out(R2), .sel(Rt));
  // also tied to GND on the sheet: {demultiplexer_1_out8[0], demultiplexer_1_out8[1], demultiplexer_1_out8[2], demultiplexer_1_out8[3], demultiplexer_1_out8[4], demultiplexer_1_out8[5], demultiplexer_1_out8[6], demultiplexer_1_out8[7], demultiplexer_1_out8[8], demultiplexer_1_out8[9], demultiplexer_1_out8[10], demultiplexer_1_out8[11], demultiplexer_1_out8[12], demultiplexer_1_out8[13], demultiplexer_1_out8[14], demultiplexer_1_out8[15], demultiplexer_1_out8[16], demultiplexer_1_out8[17], demultiplexer_1_out8[18], demultiplexer_1_out8[19], demultiplexer_1_out8[20], demultiplexer_1_out8[21], demultiplexer_1_out8[22], demultiplexer_1_out8[23], demultiplexer_1_out8[24], demultiplexer_1_out8[25], demultiplexer_1_out8[26], demultiplexer_1_out8[27], demultiplexer_1_out8[28], demultiplexer_1_out8[29], demultiplexer_1_out8[30], demultiplexer_1_out8[31], demultiplexer_2_out8, register_5_q[0], register_5_q[1], register_5_q[2], register_5_q[3], register_5_q[4], register_5_q[5], register_5_q[6], register_5_q[7], register_5_q[8], register_5_q[9], register_5_q[10], register_5_q[11], register_5_q[12], register_5_q[13], register_5_q[14], register_5_q[15], register_5_q[16], register_5_q[17], register_5_q[18], register_5_q[19], register_5_q[20], register_5_q[21], register_5_q[22], register_5_q[23], register_5_q[24], register_5_q[25], register_5_q[26], register_5_q[27], register_5_q[28], register_5_q[29], register_5_q[30], register_5_q[31]}
endmodule

module My_ALU (
  input  [31:0] X,
  input  [31:0] Y,
  input  [3:0] in_3,
  output [31:0] out_4,
  output [31:0] out_5,
  output out_6
);

  wire [0:0] comparator_1_lt, comparator_2_lt;
  wire [31:0] adder_1_out, and_1_out, divider_1_out, divider_1_rem, multiplier_1_cout, multiplier_1_out,
       nor_1_out, or_1_out, subtractor_1_out, xor_1_out;

  Multiplier #(.width(32)) multiplier_1 (.a(X), .b(Y), .out(multiplier_1_out), .cout(multiplier_1_cout));  // open: cin
  Divider #(.width(32)) divider_1 (.a(X), .b(Y), .out(divider_1_out), .rem(divider_1_rem));  // open: upper
  Adder #(.width(32)) adder_1 (.a(X), .b(Y), .out(adder_1_out));  // open: cin, cout
  Subtractor #(.width(32)) subtractor_1 (.a(X), .b(Y), .out(subtractor_1_out));  // open: bin, bout
  assign and_1_out = X & Y;  // AND_Gate and_1, 32 bits wide
  assign or_1_out = X;  // OR_Gate or_1, 32 bits wide OR_Gate
  assign xor_1_out = X ^ Y;  // XOR_Gate xor_1, 32 bits wide
  assign nor_1_out = ~(X | Y);  // NOR_Gate nor_1, 32 bits wide
  Comparator #(.width(32), .mode("twosComplement")) comparator_1 (
    .a(X), .b(Y), .eq(out_6), .lt(comparator_1_lt[0]));  // open: gt
  Comparator #(.width(32), .mode("twosComplement")) comparator_2 (
    .a(X), .b(Y), .lt(comparator_2_lt[0]));  // open: gt, eq
  Multiplexer #(.select(4), .width(32), .disabled("Z"), .enable("false")) multiplexer_1 (
    .in0({32{1'b0}}), .in1({32{1'b0}}), .in2({32{1'b0}}), .in3(multiplier_1_out), .in4(divider_1_out),
    .in5(adder_1_out), .in6(subtractor_1_out), .in7(and_1_out), .in8(or_1_out), .in9(xor_1_out),
    .in10(nor_1_out), .in11({{31{1'b0}}, comparator_1_lt[0]}), .in12({{31{1'b0}}, comparator_2_lt[0]}),
    .in13({32{1'b0}}), .in14({32{1'b0}}), .in15({32{1'b0}}), .out(out_4), .sel(in_3));
  Multiplexer #(.select(4), .width(32), .disabled("Z"), .enable("false")) multiplexer_2 (
    .in0({32{1'b0}}), .in1({32{1'b0}}), .in2({32{1'b0}}), .in3(multiplier_1_cout), .in4(divider_1_rem),
    .in5({32{1'b0}}), .in6({32{1'b0}}), .in7({32{1'b0}}), .in8({32{1'b0}}), .in9({32{1'b0}}),
    .in10({32{1'b0}}), .in11({32{1'b0}}), .in12({32{1'b0}}), .in13({32{1'b0}}), .in14({32{1'b0}}),
    .in15({32{1'b0}}), .out(out_5), .sel(in_3));

  // Other names for the same wires on the sheet: equal = out_6; opCode[3:0] = in_3; result1[31:0] = out_4;
  //   result2[31:0] = out_5
endmodule
